# Fritzing sketch Huzzle_ScreenButtonSensor_Wiring (saved by Fritzing 0.9.8b)
breadboards: 1

parts:
  WeMos_D1_Mini1 = WeMos D1 Mini
  Nokia_5110_LCD_Module1 = Nokia 5110 LCD
  Part1 = Flora TCS34725 Color Sensor
  S1 = Pushbutton [package=THT]

nets:
  3V3: WeMos_D1_Mini1.3V3, Nokia_5110_LCD_Module1.VCC, S1.leg0
  N1: WeMos_D1_Mini1.A0, S1.leg1
  N2: WeMos_D1_Mini1.D0, Part1.3.3V
  N3: WeMos_D1_Mini1.D1, Part1.SCL
  N4: WeMos_D1_Mini1.D2, Part1.SDA
  N5: WeMos_D1_Mini1.D3, Nokia_5110_LCD_Module1.RST
  N6: WeMos_D1_Mini1.D4, Nokia_5110_LCD_Module1.CE
  N7: WeMos_D1_Mini1.D5, Nokia_5110_LCD_Module1.CLK
  N8: WeMos_D1_Mini1.D6, Nokia_5110_LCD_Module1.BL
  N9: WeMos_D1_Mini1.D7, Nokia_5110_LCD_Module1.Din
  N10: WeMos_D1_Mini1.D8, Nokia_5110_LCD_Module1.D/C
  GND: WeMos_D1_Mini1.G, Nokia_5110_LCD_Module1.GND, Part1.GND

custom parts:
  Nokia 5110 LCD: Nokia 5110 Graphic 84*48 LCD module <Blue Version>
  Flora TCS34725 Color Sensor: Your electronics can now see in dazzling color with this lovely color light sensor. We found the best color sensor on the market, the TCS34725, which has RGB and Clear light sensing elements. An IR blocking filter, integrated on-chip and localized to the color sensing photodiodes, minimizes the IR spectral component of the incoming light and allows color measurements to be made accurately. The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
