# Fritzing sketch Nuzzle_KeypadLedButton_Wiring (saved by Fritzing 0.9.8b)
breadboards: 1

parts:
  WeMos_D1_Mini1 = WeMos D1 Mini
  kEYPAD_MATRICIAL_1 = KEYPAD 4x3
  LED1 = LED - 5mm [color="Red (633nm)" current=0.030 package="5 mm [THT]"]  # not connected
  LED2 = LED - 5mm [color="White (4500K)" current=0.030 package="5 mm [THT]"]  # not connected
  S1 = Pushbutton [package=THT]  # not connected

nets:
  N1: WeMos_D1_Mini1.D1, kEYPAD_MATRICIAL_1.col2
  N2: WeMos_D1_Mini1.D2, kEYPAD_MATRICIAL_1.col1
  N3: WeMos_D1_Mini1.D3, kEYPAD_MATRICIAL_1.arrow1
  N4: WeMos_D1_Mini1.D4, kEYPAD_MATRICIAL_1.arrow4
  N5: WeMos_D1_Mini1.D5, kEYPAD_MATRICIAL_1.col3
  N6: WeMos_D1_Mini1.D6, kEYPAD_MATRICIAL_1.arrow2
  N7: WeMos_D1_Mini1.D7, kEYPAD_MATRICIAL_1.arrow3

custom parts:
  KEYPAD 4x3: KEYPAD matricial de 12 botones, 4 filas x 3 columnas
